# Fritzing sketch pi-weather-station (saved by Fritzing 0.9.3b)
breadboards: 1

parts:
  Part1 = Adafruit Ultimate GPS HAT [part_number="Adafruit #2324"]
  Raspberry_Pi1 = Raspberry Pi 2  # not connected
  DHT1 = DHT22 Humidity and Temperature Sensor
  Part2 = Adafruit BME280
  R1 = Resistor [tolerance=±5% resistance=10k package="0402 [SMD]"]
  ANT1 = Antenna  # not connected
  Part3 = Adafruit TSL2561 [part_number="Adafruit #439"]

nets:
  N1: Part1.SDA, Part2.SDI/SDA, Part3.SDA
  N2: Part1.SCL, Part2.SCK/SCL, Part3.SCL
  N3: Part1.GPIO17, DHT1.DATA, R1.Pin_0
  VIN: Part1.3.3V, DHT1.VDD, Part2.VIN, R1.Pin_1, Part3.VIN
  GND: Part1.GND, DHT1.GND, Part2.GND, Part3.GND

custom parts:
  Adafruit Ultimate GPS HAT: It's 10PM, do you know where your Raspberry Pi is? If you had this GPS HAT, you would! This new HAT from Adafruit adds our celebrated Ultimate GPS on it, so you can add precision time and location to your Raspberry Pi Model A+, B+, or Pi 2. Does not work with the Pi 3 at this time Here's the low-down on the GPS module: -165 dBm sensitivity, 10 Hz updates, 66 channels Only 20mA current draw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
  Adafruit BME280: Bosch has stepped up their game with their new BME280 sensor, an environmental sensor with temperature, barometric pressure and humidity! This sensor is great for all sorts of weather/environmental sensing and can even be used in both I2C and SPI! This precision sensor from Bosch is the best low-cost sensing solution for measuring humidity with ±3% accuracy, barometric pressure with ±1 hPa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
  Adafruit TSL2561: The TSL2561 luminosity sensor is an advanced digital light sensor, ideal for use in a wide range of light situations. Compared to low cost CdS cells, this sensor is more precise, allowing for exact lux calculations and can be configured for different gain/timing ranges to detect light ranges from up to 0.1 - 40,000+ Lux on the fly. The best part of this sensor is that it contains both infrared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
